# Fritzing sketch receiver (saved by Fritzing 0.9.2b)
circuit board: 2.38923cm x 3.60653cm
breadboards: 1

parts:
  RJ45 = RJ45 Jack [package=rj45-8]
  MAX485 = MAX485 [package=dil08]
  R-7850 = Voltage Regulator - 5V [package="TO220 [THT]"]
  LED = Header 3 [package=molex-1x3_lock]
  R2 = Resistor [tolerance=±5% resistance=220 package=THT]
  R1 = Resistor [tolerance=±5% resistance=220 package=THT]
  R3 = Resistor [tolerance=±5% resistance=220 package=THT]
  R4 = Resistor [tolerance=±5% resistance=220 package=THT]

nets:
  N1: RJ45.1, MAX485.A, R1.Pin_1, R3.Pin_0
  N2: RJ45.2, MAX485.B, R2.Pin_1, R1.Pin_0
  N3: RJ45.4, RJ45.6, RJ45.8, R-7850.input_voltage
  N4: MAX485.RO, R4.Pin_0
  N5: MAX485.VCC, R-7850.output_voltage, LED.1, R3.Pin_1
  N6: LED.3, R4.Pin_1

notes:
  WS2812
  Extension
  ©CC-by
  T. Theuer
  DO NOT CONNECT
  TO NETWORK
  git.io/vwEQP
